# Fritzing sketch wiring-diagram (saved by Fritzing 0.9.3b)
breadboards: 1

parts:
  Raspberry_Pi1 = Raspberry Pi 2
  LED1 = LED - 3mm [color="Red (633nm)" package="3 mm [THT]"]
  R1 = Resistor [tolerance=±5% resistance=1k package=THT]

nets:
  N1: Raspberry_Pi1.GPIO23, R1.Pin_0
  N2: Raspberry_Pi1.GND, LED1.anode
  N3: LED1.cathode, R1.Pin_1
